// Logisim project Control Unit.circ as structural Verilog
// \
module Control_Unit_2 (
  input  CLK,
  input  READ_RAM,
  input  [3:0] Read_Time,
  input  HALT,
  input  RST,
  input  WRITE_RAM,
  input  [3:0] Write_Time,
  output E_PC,
  output END,
  output Read_RAM_2,
  output CS,
  output PC_ADDRESS,
  output R_W_RAM,
  output E_INST
);

  wire Chrono1_Reset, Chrono2_Reset, chronometer_1_finish, d_ff_1_q, d_ff_5_q, demultiplexer_2_out0,
       demultiplexer_2_out1, demultiplexer_3_out1, demultiplexer_4_out0, demultiplexer_5_out0,
       demultiplexer_5_out1, demultiplexer_6_out0, demultiplexer_7_out0, demultiplexer_7_out1,
       demultiplexer_8_out0, demultiplexer_8_out1, Execute, Execute_Finished, Execute_In_Progress, Executed,
       Fetch, Fetched, Halt_Instruction, Halt_State, Idle_Finished, or_3_out, or_4_out, or_7_out, or_10_out,
       or_11_out, or_12_out, or_13_out, R_W_Done, RAM, Start, undriven, undriven_2;
  wire [3:0] multiplexer_1_out;

  D_Flip_Flop d_ff_1 (.clk(CLK), .D(demultiplexer_3_out1), .Q(d_ff_1_q), .preset(RST));  // open: Qn, en, reset
  Demultiplexer #(.enable("false")) demultiplexer_1 (
    .out0(Execute_Finished), .out1(Chrono2_Reset), .in(Execute_In_Progress), .sel(RAM));
  Multiplexer #(.width(4), .enable("false")) multiplexer_1 (
    .in0(Read_Time), .in1(Write_Time), .out(multiplexer_1_out), .sel(WRITE_RAM));
  Demultiplexer #(.enable("false")) demultiplexer_2 (
    .out0(demultiplexer_2_out0), .out1(demultiplexer_2_out1), .in(demultiplexer_2_out0), .sel(Start));
  or or_1 (E_PC, R_W_Done, Execute_Finished);
  or or_2 (CS, Fetch, Execute);
  Demultiplexer #(.enable("false")) demultiplexer_3 (
    .out0(Idle_Finished), .out1(demultiplexer_3_out1), .in(d_ff_1_q), .sel(RST));
  or or_3 (or_3_out, demultiplexer_4_out0, Chrono2_Reset);
  Chronometer chronometer_1 (.in_1(multiplexer_1_out), .in_2(Chrono2_Reset), .in_3(CLK), .Finish(chronometer_1_finish));
  or or_4 (or_4_out, demultiplexer_5_out0, demultiplexer_8_out1, demultiplexer_2_out1);
  D_Flip_Flop d_ff_2 (.clk(CLK), .D(or_3_out), .Q(Execute), .reset(RST));  // open: Qn, preset, en
  or or_5 (R_W_RAM, WRITE_RAM, Execute);
  or or_6 (PC_ADDRESS, Fetch, Chrono1_Reset, E_PC);
  Demultiplexer #(.enable("false")) demultiplexer_4 (
    .out0(demultiplexer_4_out0), .out1(Read_RAM_2), .in(Execute), .sel(chronometer_1_finish));
  or or_7 (or_7_out, demultiplexer_6_out0, Chrono1_Reset, Idle_Finished);
  or or_8 (RAM, WRITE_RAM, READ_RAM);
  Demultiplexer #(.enable("false")) demultiplexer_5 (
    .out0(demultiplexer_5_out0), .out1(demultiplexer_5_out1), .in(or_4_out));  // open: sel
  D_Flip_Flop d_ff_3 (.clk(CLK), .D(or_7_out), .Q(Fetch), .reset(RST));  // open: Qn, preset, en
  D_Flip_Flop d_ff_4 (.clk(CLK), .D(Read_RAM_2), .Q(R_W_Done), .reset(RST));  // open: Qn, preset, en
  or or_9 (Chrono1_Reset, Execute_Finished, R_W_Done);
  Demultiplexer #(.enable("false")) demultiplexer_6 (
    .out0(demultiplexer_6_out0), .out1(E_INST), .in(Fetch), .sel(Fetched));
  Demultiplexer #(.enable("false")) demultiplexer_7 (
    .out0(demultiplexer_7_out0), .out1(demultiplexer_7_out1), .in(demultiplexer_5_out1),
    .sel(Halt_Instruction));
  or or_10 (or_10_out, demultiplexer_8_out0, demultiplexer_7_out0);
  Chronometer chronometer_2 (.in_1(Read_Time), .in_2(or_11_out), .in_3(CLK), .Finish(Fetched));
  or or_11 (or_11_out, Idle_Finished, Chrono1_Reset);
  Demultiplexer demultiplexer_8 (
    .out0(demultiplexer_8_out0), .out1(demultiplexer_8_out1), .in(or_10_out), .en(Executed));  // open: sel
  D_Flip_Flop d_ff_5 (.clk(CLK), .D(E_INST), .Q(d_ff_5_q), .reset(RST));  // open: Qn, preset, en
  Demultiplexer #(.enable("false")) demultiplexer_9 (
    .out0(Execute_In_Progress), .out1(Halt_State), .in(d_ff_5_q), .sel(HALT));
  or or_12 (or_12_out, undriven, undriven_2);
  or or_13 (or_13_out, END, Halt_State);
  D_Flip_Flop d_ff_6 (.clk(CLK), .D(or_13_out), .Q(END), .reset(RST));  // open: Qn, preset, en

  // Other names for the same wires on the sheet: Clock = CLK; Enable_PC = E_PC; Enable_Instruction = E_INST;
  //   Fecth_Finished = E_INST; Initial_Chrono_Reset = Idle_Finished; R_W_Execution = Chrono2_Reset;
  //   Read_End = Read_RAM_2; Reset = RST

  // Notes on the sheet:
  //   Iddle
  //   Inputs
  //   Outputs
  //   Idle
  //   Execution Progress
  //   Capturar Instruccion
  //   Fetch
  //   Esquema de guia
  //   Execute
  //   Fetch Progress
  //   Execute
  //   Captura Instruccion
  //   Ejecuta Instruccion 
  //   End
  //   CS
  //   End
endmodule

module Chronometer (
  input  [3:0] in_1,
  input  in_2,
  input  in_3,
  output Finish
);

  wire [3:0] counter_1_q;

  Counter #(.width(4), .max('hf)) counter_1 (
    .count(1'b1), .Q(counter_1_q), .clk(in_3), .clr(in_2));  // open: load, D, carry
  Comparator #(.width(4)) comparator_1 (.a(in_1), .b(counter_1_q), .eq(Finish));  // open: gt, lt

  // Other names for the same wires on the sheet: Clock = in_3; Reset = in_2; Time[3:0] = in_1

  // Notes on the sheet:
  //   Inputs
  //   Output
endmodule
