// Logisim project Converter_LE-BE.circ as structural Verilog: 1 circuit, main circuit Little_Endian to Big_Endian
module Little_Endian_to_Big_Endian (
  input  [31:0] Input,
  output [31:0] Output
);


  assign Output = {Input[7:0], Input[15:8], Input[23:16], Input[31:24]};
endmodule
