// Logisim project Data_Path.circ as structural Verilog
// ADD
module Data_Path_2 (
  input  CLK,
  input  [31:0] RAM_DATA,
  input  RST,
  input  E_PC,
  input  ENABLE_INSTRUCTION,
  input  READ_RAM,
  input  KBD_AVAIL,
  input  [6:0] KEYBOARD,
  input  PC_ADDRESS,
  input  [31:0] PC,
  input  [15:0] CONSTANTE,
  input  [4:0] RS,
  input  [4:0] RT,
  input  [4:0] RD,
  input  ADD,
  input  XOR,
  input  SUB,
  input  SLT,
  input  POP,
  input  SLTU,
  input  PUSH,
  input  MFHI,
  input  TTY,
  input  MFLO,
  input  MULT,
  input  TYPE_I,
  input  MULU,
  input  ADDI,
  input  RND,
  input  ANDI,
  input  KBD,
  input  ORI,
  input  DIV,
  input  XORI,
  input  DIVU,
  input  SLTI,
  input  AND,
  input  SLTIU,
  input  OR,
  input  LW,
  input  NOR,
  input  SW,
  output [31:0] RAM_WRITE_DATA,
  output [31:0] RAM_ADDRESS,
  output [31:0] INSTRUCTION,
  output [31:0] RS_2,
  output [6:0] TTY_DATA,
  output RS_____RT,
  output RS____0,
  output RS____0_2
);

  wire PC_RF, register_file_enablers_1_high_low_enable, W_E;
  wire [3:0] alu_input_1_alu_selector;
  wire [4:0] register_file_input_1_r1_address, register_file_input_1_r2_address, register_file_input_1_rw;
  wire [31:0] ALU, ALU_HIGH, alu_input_1_op_1, alu_input_1_op_2, register_file_input_1_data_in, RF_HIGH,
       RF_LOW, RT_t, SP;

  Register_File_Input register_file_input_1 (
    .RS(RS), .MFHI(MFHI), .RND(RND), .RT(RT), .MFLO(MFLO), .KBD(KBD), .RD(RD), .LW(LW), .POP(POP),
    .TYPE_I(TYPE_I), .CLK(CLK), .RAM(RAM_DATA), .ALU(ALU), .KEYBOARD(KEYBOARD), .KBD_AVAIL(KBD_AVAIL),
    .LOW(RF_LOW), .HIGH(RF_HIGH), .RW(register_file_input_1_rw), .DATA_IN(register_file_input_1_data_in),
    .R1_ADDRESS(register_file_input_1_r1_address), .R2_ADDRESS(register_file_input_1_r2_address));
  Register_File_Enablers register_file_enablers_1 (
    .PC_ENABLE(E_PC), .MULT(MULT), .SLTU(SLTU), .SLTIU(SLTIU), .MULU(MULU), .AND(AND), .DIV(DIV),
    .ANDI(ANDI), .DIVU(DIVU), .OR(OR), .ADD(ADD), .ORI(ORI), .ADDI(ADDI), .NOR(NOR), .SUB(SUB), .XOR(XOR),
    .SLT(SLT), .XORI(XORI), .SLTI(SLTI), .MFHI(MFLO), .RND(RND), .MFLO(MFHI), .KBD(KBD), .READ_RAM(READ_RAM),
    .LW(LW), .POP(POP), .W_E(W_E), .HIGH_LOW_ENABLE(register_file_enablers_1_high_low_enable),
    .PC_ENABLE_2(PC_RF));
  Register_File_2 register_file_1 (
    .RW(register_file_input_1_rw), .DATA_IN(register_file_input_1_data_in), .W_E(W_E),
    .R1_ADDRESS(register_file_input_1_r1_address), .R2_ADDRESS(register_file_input_1_r2_address), .CLK(CLK),
    .RST(RST), .HIGH_INPUT(ALU_HIGH), .HIGH_LOW_ENABLE(register_file_enablers_1_high_low_enable),
    .PUSH(PUSH), .POP(POP), .PROGRAM_COUNTER_ENABLE(PC_RF), .R1_OUTPUT(RS_2), .R2_OUTPUT(RT_t),
    .HIGH(RF_LOW), .LOW(RF_HIGH), .STACK_POINTER(SP));
  Register #(.width(32)) INSTRUCTION_MEMORY (
    .D(RAM_DATA), .en(ENABLE_INSTRUCTION), .Q(INSTRUCTION), .clk(CLK), .clr(RST));
  RAM_Instructions ram_instructions_1 (
    .ALU(ALU), .SP(SP), .PC(PC), .LW(LW), .SW(SW), .POP(POP), .PUSH(PUSH), .PC_INST(PC_ADDRESS),
    .DIR_RAM(RAM_ADDRESS));
  Multiplexer #(.width(32), .enable("false")) multiplexer_1 (.in0(RT_t), .in1(RS_2), .out(RAM_WRITE_DATA), .sel(PUSH));
  Alu_Input alu_input_1 (
    .ADD(ADD), .SLTU(SLTU), .ADDI(ADDI), .SLTIU(SLTIU), .AND(AND), .SUB(SUB), .ANDI(ANDI), .MULT(MULT),
    .OR(OR), .MULU(MULU), .ORI(ORI), .NOR(NOR), .DIV(DIV), .XOR(XOR), .DIVU(DIVU), .XORI(XORI), .SLT(SLT),
    .SLTI(SLTI), .ALU_SELECTOR(alu_input_1_alu_selector), .RS(RS_2), .RT(RT_t), .TYPE_I(TYPE_I),
    .CONSTANTE(CONSTANTE), .OP_1(alu_input_1_op_1), .OP_2(alu_input_1_op_2));
  ALU_2 alu_1 (
    .OP_1(alu_input_1_op_1), .OP_2(alu_input_1_op_2), .ALU_SELECTOR(alu_input_1_alu_selector), .RESULT(ALU),
    .HIGH(ALU_HIGH), .RS_____RT(RS_____RT), .RS____0(RS____0), .RS____0_2(RS____0_2));

  assign TTY_DATA = RS_2[6:0];

  // Other names for the same wires on the sheet: DATA_RAM[31:0] = RAM_DATA; DATA_WRITE_RAM[31:0] = RAM_WRITE_DATA;
  //   DIR_RAM[31:0] = RAM_ADDRESS; RS____0_t = RS____0_2; RS_t[31:0] = RS_2

  // Notes on the sheet:
  //   INSTRUCTIONS
  //   INPUTS
  //   OUTPUTS
  //   FLAGS
endmodule

module Program_Counter_2 (
  input  [31:0] Branch_Control,
  input  Reset,
  input  Enabled,
  input  Clock,
  output [31:0] Instruction
);

  Register #(.width(32)) PC (.D(Branch_Control), .en(Enabled), .Q(Instruction), .clk(Clock), .clr(Reset));
endmodule

module Register_File_Input (
  input  [4:0] RS,
  input  MFHI,
  input  RND,
  input  [4:0] RT,
  input  MFLO,
  input  KBD,
  input  [4:0] RD,
  input  LW,
  input  POP,
  input  TYPE_I,
  input  CLK,
  input  [31:0] RAM,
  input  [31:0] ALU,
  input  [6:0] KEYBOARD,
  input  KBD_AVAIL,
  input  [31:0] LOW,
  input  [31:0] HIGH,
  output [4:0] RW,
  output [31:0] DATA_IN,
  output [4:0] R1_ADDRESS,
  output [4:0] R2_ADDRESS
);

  wire ALU_OUT, and_1_out, not_1_out, not_2_out, or_1_out;
  wire [1:0] DATA_SELECT, priority_encoder_1_out;
  wire [31:0] KEYBOARD_OUTPUT, KEYBOARD_t, multiplexer_4_out, multiplexer_5_out, RANDOM;

  assign KEYBOARD_t = {{25{1'b0}}, KEYBOARD};  // Bit_Extender bit_extender_1
  Priority_Encoder #(.select(2)) priority_encoder_1 (
    .in0(MFHI), .in1(MFLO), .in2(RND), .in3(KBD), .out(priority_encoder_1_out), .en_out(ALU_OUT));  // open: gs, en_in
  Multiplexer #(.width(2), .enable("false")) multiplexer_1 (
    .in0(priority_encoder_1_out), .in1(2'b00), .out(DATA_SELECT), .sel(ALU_OUT));
  Multiplexer #(.width(32), .enable("false")) multiplexer_2 (
    .in0({32{1'b1}}), .in1(KEYBOARD_t), .out(KEYBOARD_OUTPUT), .sel(KBD_AVAIL));
  Random #(.width(32)) random_1 (.clk(CLK), .next(RND), .out(RANDOM));  // open: clr
  Multiplexer #(.width(5), .enable("false")) multiplexer_3 (.in0(RD), .in1(RT), .out(RW), .sel(TYPE_I));
  Multiplexer #(.select(2), .width(32), .enable("false")) multiplexer_4 (
    .in0(HIGH), .in1(LOW), .in2(RANDOM), .in3(KEYBOARD_OUTPUT), .out(multiplexer_4_out), .sel(DATA_SELECT));
  Multiplexer #(.width(32), .enable("false")) multiplexer_5 (
    .in0(multiplexer_4_out), .in1(RAM), .out(multiplexer_5_out), .sel(or_1_out));
  or or_1 (or_1_out, LW, POP);
  Multiplexer #(.width(32), .enable("false")) multiplexer_6 (
    .in0(multiplexer_5_out), .in1(ALU), .out(DATA_IN), .sel(and_1_out));
  and and_1 (and_1_out, not_1_out, not_2_out, ALU_OUT);
  not not_1 (not_1_out, POP);
  not not_2 (not_2_out, LW);

  assign R1_ADDRESS = RS;
  assign R2_ADDRESS = RT;

  // Other names for the same wires on the sheet: D_IN[31:0] = DATA_IN

  // Notes on the sheet:
  //   INPUTS
  //   REGISTER_WRITE
  //   KEYBOARD
  //   RANDOM
  //   DATA_INPUT
  //   OUTPUTS
  //   REGISTER_WRITE
  //   DATA_IN
  //   R1_ADDRESS
  //   R2_ADDRESS
endmodule

module Register_File_Enablers (
  input  PC_ENABLE,
  input  MULT,
  input  SLTU,
  input  SLTIU,
  input  MULU,
  input  AND,
  input  DIV,
  input  ANDI,
  input  DIVU,
  input  OR,
  input  ADD,
  input  ORI,
  input  ADDI,
  input  NOR,
  input  SUB,
  input  XOR,
  input  SLT,
  input  XORI,
  input  SLTI,
  input  MFHI,
  input  RND,
  input  MFLO,
  input  KBD,
  input  READ_RAM,
  input  LW,
  input  POP,
  output W_E,
  output HIGH_LOW_ENABLE,
  output PC_ENABLE_2
);

  wire ADD_t, AND_t, or_7_out, OR_t, PC_TYPE, priority_encoder_2_gs, priority_encoder_3_gs,
       priority_encoder_4_gs, priority_encoder_5_gs, RAM_TYPE, SLT_t, SLTU_t, XOR_t;

  or or_1 (ADD_t, ADD, ADDI);
  or or_2 (SLT_t, SLT, SLTI);
  or or_3 (SLTU_t, SLTU, SLTIU);
  or or_4 (AND_t, AND, ANDI);
  or or_5 (OR_t, OR, ORI);
  or or_6 (XOR_t, XOR, XORI);
  Priority_Encoder #(.select(2)) priority_encoder_1 (
    .in0(MULT), .in1(MULU), .in2(DIV), .in3(DIVU), .gs(HIGH_LOW_ENABLE));  // open: out, en_out, en_in
  Priority_Encoder #(.select(2)) priority_encoder_2 (
    .in0(ADD_t), .in1(SUB), .in2(SLT_t), .in3(SLTU_t), .gs(priority_encoder_2_gs));  // open: out, en_out, en_in
  Priority_Encoder #(.select(2)) priority_encoder_3 (
    .in0(AND_t), .in1(OR_t), .in2(NOR), .in3(XOR_t), .gs(priority_encoder_3_gs));  // open: out, en_out, en_in
  Priority_Encoder #(.select(2)) priority_encoder_4 (
    .in0(MFHI), .in1(MFLO), .in2(RND), .in3(KBD), .gs(priority_encoder_4_gs));  // open: out, en_out, en_in
  or or_7 (or_7_out, LW, POP);
  and and_1 (RAM_TYPE, or_7_out, READ_RAM);
  Priority_Encoder #(.select(2)) priority_encoder_5 (
    .in0(HIGH_LOW_ENABLE), .in1(priority_encoder_2_gs), .in2(priority_encoder_3_gs),
    .in3(priority_encoder_4_gs), .gs(priority_encoder_5_gs));  // open: out, en_out, en_in
  and and_2 (PC_TYPE, PC_ENABLE, priority_encoder_5_gs);
  or or_8 (W_E, PC_TYPE, RAM_TYPE);

  assign PC_ENABLE_2 = PC_ENABLE;

  // Notes on the sheet:
  //   PC_TYPE
  //   RAM_TYPE
  //   INPUTS
  //   OUTPUTS
  //   WRITE_ENABLE
endmodule

module Register_File_2 (
  input  [4:0] RW,
  input  [31:0] DATA_IN,
  input  W_E,
  input  [4:0] R1_ADDRESS,
  input  [4:0] R2_ADDRESS,
  input  CLK,
  input  RST,
  input  [31:0] HIGH_INPUT,
  input  HIGH_LOW_ENABLE,
  input  PUSH,
  input  POP,
  input  PROGRAM_COUNTER_ENABLE,
  output [31:0] R1_OUTPUT,
  output [31:0] R2_OUTPUT,
  output [31:0] HIGH,
  output [31:0] LOW,
  output [31:0] STACK_POINTER
);

  wire and_1_out, BANK0_SELECT, BANK1_SELECT, BANK2_SELECT, BANK3_SELECT, or_1_out, R1_WRITE, R2_WRITE,
       R3_WRITE, R4_WRITE, R5_WRITE, R6_WRITE, R7_WRITE, R8_WRITE, R9_WRITE, R10_WRITE, R11_WRITE, R12_WRITE,
       R13_WRITE, R14_WRITE, R15_WRITE, R16_WRITE, R17_WRITE, R18_WRITE, R19_WRITE, R20_WRITE, R21_WRITE,
       R22_WRITE, R23_WRITE, R24_WRITE, R25_WRITE, R26_WRITE, R27_WRITE, R28_WRITE, R29_WRITE, R30_WRITE,
       R31_WRITE, STACK_POINTER_WRITE;
  wire [31:0] multiplexer_1_out, multiplexer_2_out, multiplexer_3_out, multiplexer_4_out, multiplexer_6_out,
       multiplexer_7_out, multiplexer_8_out, multiplexer_9_out, multiplexer_11_out, R0, R1, R2, R3, R4, R5,
       R6, R7, R8, R9, R10, R11, R12, R13, R14, R15, R16, R17, R18, R19, R20, R21, R22, R23, R24, R25, R26,
       R27, R28, R29, R30, STACK_POINTER___4, STACK_POINTER___4_t, STACK_POINTER_INPUT;

  Register #(.width(32)) zero (.D({32{1'b0}}), .Q(R0), .clk(CLK), .clr(RST));  // open: en
  Register #(.width(32)) t0 (.D(DATA_IN), .en(R8_WRITE), .Q(R8), .clk(CLK), .clr(RST));
  Register #(.width(32)) s0 (.D(DATA_IN), .en(R16_WRITE), .Q(R16), .clk(CLK), .clr(RST));
  Register #(.width(32)) t8 (.D(DATA_IN), .en(R24_WRITE), .Q(R24), .clk(CLK), .clr(RST));
  Multiplexer #(.select(3), .width(32), .disabled(0), .enable("false")) multiplexer_1 (
    .in0(R0), .in1(R1), .in2(R2), .in3(R3), .in4(R4), .in5(R5), .in6(R6), .in7(R7), .out(multiplexer_1_out),
    .sel(R1_ADDRESS[2:0]));
  Multiplexer #(.select(3), .width(32), .disabled(0), .enable("false")) multiplexer_2 (
    .in0(R8), .in1(R9), .in2(R10), .in3(R11), .in4(R12), .in5(R13), .in6(R14), .in7(R15),
    .out(multiplexer_2_out), .sel(R1_ADDRESS[2:0]));
  Multiplexer #(.select(3), .width(32), .disabled(0), .enable("false")) multiplexer_3 (
    .in0(R16), .in1(R17), .in2(R18), .in3(R19), .in4(R20), .in5(R21), .in6(R22), .in7(R23),
    .out(multiplexer_3_out), .sel(R1_ADDRESS[2:0]));
  Multiplexer #(.select(3), .width(32), .disabled(0), .enable("false")) multiplexer_4 (
    .in0(R24), .in1(R25), .in2(R26), .in3(R27), .in4(R28), .in5(R29), .in6(R30), .in7(STACK_POINTER),
    .out(multiplexer_4_out), .sel(R1_ADDRESS[2:0]));
  Register #(.width(32)) at (.D(DATA_IN), .en(R1_WRITE), .Q(R1), .clk(CLK), .clr(RST));
  Register #(.width(32)) t1 (.D(DATA_IN), .en(R9_WRITE), .Q(R9), .clk(CLK), .clr(RST));
  Register #(.width(32)) s1 (.D(DATA_IN), .en(R17_WRITE), .Q(R17), .clk(CLK), .clr(RST));
  Register #(.width(32)) t9 (.D(DATA_IN), .en(R25_WRITE), .Q(R25), .clk(CLK), .clr(RST));
  Demultiplexer #(.select(3), .disabled(0)) demultiplexer_1 (
    .out1(R1_WRITE), .out2(R2_WRITE), .out3(R3_WRITE), .out4(R4_WRITE), .out5(R5_WRITE), .out6(R6_WRITE),
    .out7(R7_WRITE), .in(1'b1), .sel(RW[2:0]), .en(BANK0_SELECT));  // open: out0
  Demultiplexer #(.select(3), .disabled(0)) demultiplexer_2 (
    .out0(R16_WRITE), .out1(R17_WRITE), .out2(R18_WRITE), .out3(R19_WRITE), .out4(R20_WRITE),
    .out5(R21_WRITE), .out6(R22_WRITE), .out7(R23_WRITE), .in(1'b1), .sel(RW[2:0]), .en(BANK2_SELECT));
  Multiplexer #(.select(2), .width(32), .enable("false")) multiplexer_5 (
    .in0(multiplexer_1_out), .in1(multiplexer_2_out), .in2(multiplexer_3_out), .in3(multiplexer_4_out),
    .out(R1_OUTPUT), .sel(R1_ADDRESS[4:3]));
  Demultiplexer #(.select(2), .disabled(0)) demultiplexer_3 (
    .out0(BANK0_SELECT), .out1(BANK1_SELECT), .out2(BANK2_SELECT), .out3(BANK3_SELECT), .in(1'b1),
    .sel(RW[4:3]), .en(W_E));
  Register #(.width(32)) v0 (.D(DATA_IN), .en(R2_WRITE), .Q(R2), .clk(CLK), .clr(RST));
  Register #(.width(32)) t2 (.D(DATA_IN), .en(R10_WRITE), .Q(R10), .clk(CLK), .clr(RST));
  Register #(.width(32)) s2 (.D(DATA_IN), .en(R18_WRITE), .Q(R18), .clk(CLK), .clr(RST));
  Register #(.width(32)) t10 (.D(DATA_IN), .en(R26_WRITE), .Q(R26), .clk(CLK), .clr(RST));
  Demultiplexer #(.select(3), .disabled(0)) demultiplexer_4 (
    .out0(R8_WRITE), .out1(R9_WRITE), .out2(R10_WRITE), .out3(R11_WRITE), .out4(R12_WRITE), .out5(R13_WRITE),
    .out6(R14_WRITE), .out7(R15_WRITE), .in(1'b1), .sel(RW[2:0]), .en(BANK1_SELECT));
  Demultiplexer #(.select(3), .disabled(0)) demultiplexer_5 (
    .out0(R24_WRITE), .out1(R25_WRITE), .out2(R26_WRITE), .out3(R27_WRITE), .out4(R28_WRITE),
    .out5(R29_WRITE), .out6(R30_WRITE), .out7(R31_WRITE), .in(1'b1), .sel(RW[2:0]), .en(BANK3_SELECT));
  Register #(.width(32)) v1 (.D(DATA_IN), .en(R3_WRITE), .Q(R3), .clk(CLK), .clr(RST));
  Register #(.width(32)) t3 (.D(DATA_IN), .en(R11_WRITE), .Q(R11), .clk(CLK), .clr(RST));
  Register #(.width(32)) s3 (.D(DATA_IN), .en(R19_WRITE), .Q(R19), .clk(CLK), .clr(RST));
  Register #(.width(32)) t11 (.D(DATA_IN), .en(R27_WRITE), .Q(R27), .clk(CLK), .clr(RST));
  Multiplexer #(.select(3), .width(32), .disabled(0), .enable("false")) multiplexer_6 (
    .in0(R0), .in1(R1), .in2(R2), .in3(R3), .in4(R4), .in5(R5), .in6(R6), .in7(R7), .out(multiplexer_6_out),
    .sel(R2_ADDRESS[2:0]));
  Multiplexer #(.select(3), .width(32), .disabled(0), .enable("false")) multiplexer_7 (
    .in0(R8), .in1(R9), .in2(R10), .in3(R11), .in4(R12), .in5(R13), .in6(R14), .in7(R15),
    .out(multiplexer_7_out), .sel(R2_ADDRESS[2:0]));
  Multiplexer #(.select(3), .width(32), .disabled(0), .enable("false")) multiplexer_8 (
    .in0(R16), .in1(R17), .in2(R18), .in3(R19), .in4(R20), .in5(R21), .in6(R22), .in7(R23),
    .out(multiplexer_8_out), .sel(R2_ADDRESS[2:0]));
  Multiplexer #(.select(3), .width(32), .disabled(0), .enable("false")) multiplexer_9 (
    .in0(R24), .in1(R25), .in2(R26), .in3(R27), .in4(R28), .in5(R29), .in6(R30), .in7(STACK_POINTER),
    .out(multiplexer_9_out), .sel(R2_ADDRESS[2:0]));
  Register #(.width(32)) a0 (.D(DATA_IN), .en(R4_WRITE), .Q(R4), .clk(CLK), .clr(RST));
  Register #(.width(32)) t4 (.D(DATA_IN), .en(R12_WRITE), .Q(R12), .clk(CLK), .clr(RST));
  Register #(.width(32)) s4 (.D(DATA_IN), .en(R20_WRITE), .Q(R20), .clk(CLK), .clr(RST));
  Register #(.width(32)) t12 (.D(DATA_IN), .en(R28_WRITE), .Q(R28), .clk(CLK), .clr(RST));
  Multiplexer #(.select(2), .width(32), .enable("false")) multiplexer_10 (
    .in0(multiplexer_6_out), .in1(multiplexer_7_out), .in2(multiplexer_8_out), .in3(multiplexer_9_out),
    .out(R2_OUTPUT), .sel(R2_ADDRESS[4:3]));
  Register #(.width(32)) a1 (.D(DATA_IN), .en(R5_WRITE), .Q(R5), .clk(CLK), .clr(RST));
  Register #(.width(32)) t5 (.D(DATA_IN), .en(R13_WRITE), .Q(R13), .clk(CLK), .clr(RST));
  Register #(.width(32)) s5 (.D(DATA_IN), .en(R21_WRITE), .Q(R21), .clk(CLK), .clr(RST));
  Register #(.width(32)) t13 (.D(DATA_IN), .en(R29_WRITE), .Q(R29), .clk(CLK), .clr(RST));
  Register #(.width(32)) u_HIGH (.D(HIGH_INPUT), .en(HIGH_LOW_ENABLE), .Q(HIGH), .clk(CLK), .clr(RST));
  Register #(.width(32)) u_LOW (.D(DATA_IN), .en(HIGH_LOW_ENABLE), .Q(LOW), .clk(CLK), .clr(RST));
  Register #(.width(32)) a2 (.D(DATA_IN), .en(R6_WRITE), .Q(R6), .clk(CLK), .clr(RST));
  Register #(.width(32)) t6 (.D(DATA_IN), .en(R14_WRITE), .Q(R14), .clk(CLK), .clr(RST));
  Register #(.width(32)) s6 (.D(DATA_IN), .en(R22_WRITE), .Q(R22), .clk(CLK), .clr(RST));
  Register #(.width(32)) t14 (.D(DATA_IN), .en(R30_WRITE), .Q(R30), .clk(CLK), .clr(RST));
  Adder #(.width(32)) adder_1 (.a(STACK_POINTER), .b(32'h4), .out(STACK_POINTER___4));  // open: cin, cout
  Subtractor #(.width(32)) subtractor_1 (.a(STACK_POINTER), .b(32'h4), .out(STACK_POINTER___4_t));  // open: bin, bout
  Multiplexer #(.width(32), .enable("false")) multiplexer_11 (
    .in0(STACK_POINTER___4_t), .in1(STACK_POINTER___4), .out(multiplexer_11_out), .sel(POP));
  or or_1 (or_1_out, POP, PUSH);
  Multiplexer #(.width(32), .enable("false")) multiplexer_12 (
    .in0(multiplexer_11_out), .in1(DATA_IN), .out(STACK_POINTER_INPUT), .sel(R31_WRITE));
  and and_1 (and_1_out, or_1_out, PROGRAM_COUNTER_ENABLE);
  Register #(.width(32)) a3 (.D(DATA_IN), .en(R7_WRITE), .Q(R7), .clk(CLK), .clr(RST));
  Register #(.width(32)) t7 (.D(DATA_IN), .en(R15_WRITE), .Q(R15), .clk(CLK), .clr(RST));
  Register #(.width(32)) s7 (.D(DATA_IN), .en(R23_WRITE), .Q(R23), .clk(CLK), .clr(RST));
  or or_2 (STACK_POINTER_WRITE, RST, and_1_out, R31_WRITE);
  Register #(.width(32)) SP (
    .D(STACK_POINTER_INPUT), .en(STACK_POINTER_WRITE), .Q(STACK_POINTER), .clk(CLK), .clr(RST));

  // Other names for the same wires on the sheet: D_IN[31:0] = DATA_IN; PC_ENABLE = PROGRAM_COUNTER_ENABLE;
  //   R1_A[4:0] = R1_ADDRESS; R1_BANK_ADDRESS[2:0] = R1_ADDRESS[2:0]; R1_BANK_SELECT[1:0] = R1_ADDRESS[4:3];
  //   R1_OUT[31:0] = R1_OUTPUT; R2_A[4:0] = R2_ADDRESS; R2_BANK_ADDRESS[2:0] = R2_ADDRESS[2:0];
  //   R2_BANK_SELECT[1:0] = R2_ADDRESS[4:3]; R2_OUT[31:0] = R2_OUTPUT; BANK_ADDRESS[2:0] = RW[2:0]

  // Notes on the sheet:
  //   INPUTS
  //   REGISTER_WRITE
  //   DATA_IN
  //   WRITE_ENABLE
  //   R1_ADDRESS
  //   R2_ADDRESS
  //   HIGH_INPUT
  //   R1_OUT
  //   BANK_0
  //   BANK_2
  //   OUTPUT_BANK_SELECT
  //   BANK_SELECT
  //   REGISTER_SELECTION
  //   BANK_1
  //   BANK_3
  //   R2_OUT
  //   OUTPUTS
  //   R1_OUTPUT
  //   R2_OUTPUT
endmodule

module Alu_Input (
  input  [31:0] RS,
  input  [31:0] RT,
  input  TYPE_I,
  input  [15:0] CONSTANTE,
  input  ADD,
  input  DIV,
  input  ADDI,
  input  DIVU,
  input  SUB,
  input  AND,
  input  SLT,
  input  ANDI,
  input  SLTI,
  input  OR,
  input  SLTU,
  input  ORI,
  input  SLTIU,
  input  NOR,
  input  MULT,
  input  XOR,
  input  MULU,
  input  XORI,
  output [31:0] OP_1,
  output [31:0] OP_2,
  output [3:0] ALU_SELECTOR
);

  wire ADD_t, AND_t, LOGICAL_ENABLE, or_7_out, OR_t, priority_encoder_1_en_out, SLT_t, SLTU_t, XOR_t;
  wire [1:0] priority_encoder_2_out;
  wire [2:0] bit_extender_3_out, multiplexer_2_out, priority_encoder_1_out;
  wire [3:0] ARITHMETIC, LOGICAL;
  wire [31:0] bit_extender_1_out, bit_extender_2_out, multiplexer_1_out;

  Sign_Divider sign_divider_1 ();  // open: DIVIDEND, DIVISOR, LOW, HIGH
  or or_1 (ADD_t, ADD, ADDI);
  or or_2 (SLT_t, SLT, SLTI);
  or or_3 (SLTU_t, SLTU, SLTIU);
  or or_4 (AND_t, AND, ANDI);
  or or_5 (OR_t, OR, ORI);
  or or_6 (XOR_t, XOR, XORI);
  assign bit_extender_1_out = {{16{CONSTANTE[15]}}, CONSTANTE};  // Bit_Extender bit_extender_1
  assign bit_extender_2_out = {{16{1'b0}}, CONSTANTE};  // Bit_Extender bit_extender_2
  Priority_Encoder priority_encoder_1 (
    .in0(ADD_t), .in1(SUB), .in2(SLT_t), .in3(SLTU_t), .in4(MULT), .in5(MULU), .in6(DIV), .in7(DIVU),
    .out(priority_encoder_1_out), .en_out(priority_encoder_1_en_out));  // open: en_in, gs
  Priority_Encoder #(.select(2)) priority_encoder_2 (
    .in0(AND_t), .in1(OR_t), .in2(NOR), .in3(XOR_t), .out(priority_encoder_2_out), .gs(LOGICAL_ENABLE));  // open: en_out, en_in
  assign bit_extender_3_out = {{1{1'b0}}, priority_encoder_2_out};  // Bit_Extender bit_extender_3
  Multiplexer #(.width(32), .enable("false")) multiplexer_1 (
    .in0(bit_extender_1_out), .in1(bit_extender_2_out), .out(multiplexer_1_out), .sel(or_7_out));
  or or_7 (or_7_out, ANDI, NOR, XORI);
  Multiplexer #(.width(3), .enable("false")) multiplexer_2 (
    .in0(priority_encoder_1_out), .in1(3'b000), .out(multiplexer_2_out), .sel(priority_encoder_1_en_out));
  assign LOGICAL = {{1{1'b1}}, bit_extender_3_out};  // Bit_Extender bit_extender_4
  Multiplexer #(.width(32), .enable("false")) multiplexer_3 (
    .in0(RT), .in1(multiplexer_1_out), .out(OP_2), .sel(TYPE_I));
  assign ARITHMETIC = {{1{1'b0}}, multiplexer_2_out};  // Bit_Extender bit_extender_5
  Multiplexer #(.width(4), .enable("false")) multiplexer_4 (
    .in0(ARITHMETIC), .in1(LOGICAL), .out(ALU_SELECTOR), .sel(LOGICAL_ENABLE));

  assign OP_1 = RS;

  // Notes on the sheet:
  //   INPUTS
  //   TYPE_I
  //   SELECTOR
  //   OP_2
  //   SELECTION
  //   OUTPUTS
endmodule

module ALU_2 (
  input  [31:0] OP_1,
  input  [31:0] OP_2,
  input  [3:0] ALU_SELECTOR,
  output [31:0] RESULT,
  output [31:0] HIGH,
  output RS_____RT,
  output RS____0,
  output RS____0_2
);

  wire comparator_4_eq, NEG, POS, RS____0_t_t, RS_____0, RS______RT, RS______RT_t, SLT_RESULT, SLTU_RESULT,
       ZERO;
  wire [31:0] ADD, AND, ARITHMETIC, DIV_HIGH, DIV_LOW, DIVU_HIGH, DIVU_LOW, LOGIC, MULT_HIGH, MULT_LOW,
       MULU_HIGH, MULU_LOW, NOR, OR, SLT, SLTU, SUB, XOR;

  Sign_Multiplier sign_multiplier_1 (.OP_1(OP_1), .OP_2(OP_2), .LOW(MULT_LOW), .HIGH(MULT_HIGH));
  Adder #(.width(32)) adder_1 (.a(OP_1), .b(OP_2), .out(ADD));  // open: cin, cout
  Multiplier #(.width(32)) multiplier_1 (.a(OP_1), .b(OP_2), .out(MULU_LOW), .cout(MULU_HIGH));  // open: cin
  Comparator #(.width(32)) comparator_1 (.a(OP_1), .b(OP_2), .lt(SLT_RESULT));  // open: gt, eq
  assign SLT = {{31{1'b0}}, SLT_RESULT};  // Bit_Extender bit_extender_1
  Comparator #(.width(32)) comparator_2 (.a(OP_1), .b(OP_2), .eq(RS______RT_t));  // open: gt, lt
  not not_1 (RS______RT, RS______RT_t);
  Subtractor #(.width(32)) subtractor_1 (.a(OP_1), .b(OP_2), .out(SUB));  // open: bin, bout
  Divider #(.width(32)) divider_1 (.a(OP_1), .b(OP_2), .out(DIVU_LOW), .rem(DIVU_HIGH));  // open: upper
  Sign_Divider sign_divider_1 (.DIVIDEND(OP_1), .DIVISOR(OP_2), .LOW(DIV_LOW), .HIGH(DIV_HIGH));
  Comparator #(.width(32), .mode("unsigned")) comparator_3 (.a(OP_1), .b(OP_2), .lt(SLTU_RESULT));  // open: gt, eq
  assign SLTU = {{31{1'b0}}, SLTU_RESULT};  // Bit_Extender bit_extender_2
  Comparator #(.width(32)) comparator_4 (
    .a(OP_1), .b({32{1'b0}}), .gt(RS____0_t_t), .eq(comparator_4_eq), .lt(RS____0_2));
  Multiplexer #(.select(2), .width(32)) multiplexer_1 (
    .in0(AND), .in1(OR), .in2(NOR), .in3(XOR), .out(LOGIC), .sel(ALU_SELECTOR[1:0]), .en(ALU_SELECTOR[3]));
  Multiplexer #(.width(32), .enable("false")) multiplexer_2 (
    .in0(ARITHMETIC), .in1(LOGIC), .out(RESULT), .sel(ALU_SELECTOR[3]));
  or or_1 (RS_____0, comparator_4_eq, RS____0_2);
  Multiplexer #(.select(3), .width(32), .enable("false")) multiplexer_3 (
    .in0(ADD), .in1(SUB), .in2(SLT), .in3(SLTU), .in4(MULT_LOW), .in5(MULU_LOW), .in6(DIV_LOW),
    .in7(DIVU_LOW), .out(ARITHMETIC), .sel(ALU_SELECTOR[2:0]));
  Multiplexer #(.select(2), .width(32), .enable("false")) multiplexer_4 (
    .in0(MULT_HIGH), .in1(MULU_HIGH), .in2(DIV_HIGH), .in3(DIVU_HIGH), .out(HIGH), .sel(ALU_SELECTOR[1:0]));
  Comparator #(.width(32)) comparator_5 (.a(RESULT), .b({32{1'b0}}), .gt(POS), .eq(ZERO), .lt(NEG));
  assign AND = OP_1 & OP_2;  // AND_Gate and_1, 32 bits wide
  assign OR = OP_1 | OP_2;  // OR_Gate or_2, 32 bits wide
  Priority_Encoder #(.select(1)) priority_encoder_1 (
    .in0(RS______RT), .in1(RS______RT_t), .out(RS_____RT));  // open: gs, en_out, en_in
  Priority_Encoder #(.select(1)) priority_encoder_2 (
    .in0(RS____0_t_t), .in1(RS_____0), .out(RS____0));  // open: gs, en_out, en_in
  assign NOR = ~(OP_1 | OP_2);  // NOR_Gate nor_1, 32 bits wide
  assign XOR = OP_1 ^ OP_2;  // XOR_Gate xor_1, 32 bits wide

  // Other names for the same wires on the sheet: SELECTOR___1[2:0] = ALU_SELECTOR[2:0];
  //   SELECTOR___2[1:0] = ALU_SELECTOR[1:0]; LOGICAL = ALU_SELECTOR[3]; RS____0_t = RS____0_2

  // Notes on the sheet:
  //   FLAGS
  //   INPUTS
  //   ARITMÉTICAS
  //   OUTPUTS
  //   LÓGICAS
endmodule

module Instruction_Decoder (
  input  [31:0] INSTRUCTION,
  output [25:0] DESTINO_SALTO,
  output [15:0] CONSTANTE,
  output [4:0] RS,
  output [4:0] RT,
  output [4:0] RD,
  output ADD,
  output SUB,
  output POP,
  output PUSH,
  output HALT,
  output TTY,
  output ADDI,
  output ANDI,
  output J,
  output MULT,
  output MULU,
  output ORI,
  output XORI,
  output RND,
  output KBD,
  output DIV,
  output DIVU,
  output SLTI,
  output SLTIU,
  output AND,
  output OR,
  output BEQ,
  output BNE,
  output BLEZ,
  output BGTZ,
  output TYPE_I,
  output NOR,
  output XOR,
  output BLTZ,
  output LW,
  output SLT,
  output SLTU,
  output SW,
  output MFHI,
  output MFLO,
  output NOP,
  output JR
);

  wire _00_0000, _11_1000, _11_1111, comparator_4_eq, comparator_5_eq, comparator_6_eq, comparator_7_eq,
       comparator_8_eq, comparator_13_eq, comparator_14_eq, comparator_15_eq, comparator_16_eq,
       comparator_17_eq, comparator_21_eq, comparator_22_eq, comparator_23_eq, comparator_24_eq,
       comparator_25_eq, comparator_26_eq, comparator_31_eq, comparator_32_eq, comparator_33_eq,
       comparator_34_eq, comparator_35_eq, comparator_36_eq, or_1_out, or_2_out, or_3_out;

  Comparator #(.width(6)) comparator_1 (.a(INSTRUCTION[31:26]), .b({6{1'b0}}), .eq(_00_0000));  // open: gt, lt
  Comparator #(.width(6)) comparator_2 (.a(INSTRUCTION[31:26]), .b(6'b111000), .eq(_11_1000));  // open: gt, lt
  Comparator #(.width(6)) comparator_3 (.a(INSTRUCTION[31:26]), .b({6{1'b1}}), .eq(_11_1111));  // open: gt, lt
  Comparator #(.width(6)) comparator_4 (.a(INSTRUCTION[5:0]), .b(6'b100000), .eq(comparator_4_eq));  // open: gt, lt
  Comparator #(.width(6)) comparator_5 (.a(INSTRUCTION[5:0]), .b(6'b011010), .eq(comparator_5_eq));  // open: gt, lt
  Comparator #(.width(6)) comparator_6 (.a(INSTRUCTION[5:0]), .b(6'b100111), .eq(comparator_6_eq));  // open: gt, lt
  Comparator #(.width(6)) comparator_7 (.a(INSTRUCTION[5:0]), .b(6'b010000), .eq(comparator_7_eq));  // open: gt, lt
  Comparator #(.width(6)) comparator_8 (.a(INSTRUCTION[5:0]), .b({6{1'b0}}), .eq(comparator_8_eq));  // open: gt, lt
  Comparator #(.width(6)) comparator_9 (.a(INSTRUCTION[31:26]), .b(6'b000010), .eq(J));  // open: gt, lt
  and and_1 (ADD, _00_0000, comparator_4_eq);
  and and_2 (DIV, _00_0000, comparator_5_eq);
  and and_3 (NOR, _00_0000, comparator_6_eq);
  and and_4 (MFHI, _00_0000, comparator_7_eq);
  and and_5 (POP, _11_1000, comparator_8_eq);
  Comparator #(.width(6)) comparator_10 (.a(INSTRUCTION[31:26]), .b(6'b001000), .eq(ADDI));  // open: gt, lt
  Comparator #(.width(6)) comparator_11 (.a(INSTRUCTION[31:26]), .b(6'b001010), .eq(SLTI));  // open: gt, lt
  Comparator #(.width(6)) comparator_12 (.a(INSTRUCTION[31:26]), .b(6'b000110), .eq(BLEZ));  // open: gt, lt
  Comparator #(.width(6)) comparator_13 (.a(INSTRUCTION[5:0]), .b(6'b100010), .eq(comparator_13_eq));  // open: gt, lt
  Comparator #(.width(6)) comparator_14 (.a(INSTRUCTION[5:0]), .b(6'b011011), .eq(comparator_14_eq));  // open: gt, lt
  Comparator #(.width(6)) comparator_15 (.a(INSTRUCTION[5:0]), .b(6'b101000), .eq(comparator_15_eq));  // open: gt, lt
  and and_6 (SUB, _00_0000, comparator_13_eq);
  and and_7 (DIVU, _00_0000, comparator_14_eq);
  and and_8 (XOR, _00_0000, comparator_15_eq);
  and and_9 (MFLO, _00_0000, comparator_16_eq);
  Comparator #(.width(6)) comparator_16 (.a(INSTRUCTION[5:0]), .b(6'b010010), .eq(comparator_16_eq));  // open: gt, lt
  and and_10 (PUSH, _11_1000, comparator_17_eq);
  Comparator #(.width(6)) comparator_17 (.a(INSTRUCTION[5:0]), .b(6'b000001), .eq(comparator_17_eq));  // open: gt, lt
  Comparator #(.width(6)) comparator_18 (.a(INSTRUCTION[31:26]), .b(6'b001100), .eq(ANDI));  // open: gt, lt
  Comparator #(.width(6)) comparator_19 (.a(INSTRUCTION[31:26]), .b(6'b001011), .eq(SLTIU));  // open: gt, lt
  Comparator #(.width(6)) comparator_20 (.a(INSTRUCTION[31:26]), .b(6'b000111), .eq(BGTZ));  // open: gt, lt
  Comparator #(.width(6)) comparator_21 (.a(INSTRUCTION[5:0]), .b(6'b011000), .eq(comparator_21_eq));  // open: gt, lt
  and and_11 (MULT, _00_0000, comparator_21_eq);
  Comparator #(.width(6)) comparator_22 (.a(INSTRUCTION[5:0]), .b(6'b100100), .eq(comparator_22_eq));  // open: gt, lt
  Comparator #(.width(6)) comparator_23 (.a(INSTRUCTION[5:0]), .b(6'b101010), .eq(comparator_23_eq));  // open: gt, lt
  Comparator #(.width(6)) comparator_24 (.a(INSTRUCTION[5:0]), .b({6{1'b0}}), .eq(comparator_24_eq));  // open: gt, lt
  Comparator #(.width(6)) comparator_25 (.a(INSTRUCTION[5:0]), .b({6{1'b1}}), .eq(comparator_25_eq));  // open: gt, lt
  Comparator #(.width(6)) comparator_26 (.a(INSTRUCTION[5:0]), .b(6'b000010), .eq(comparator_26_eq));  // open: gt, lt
  Comparator #(.width(6)) comparator_27 (.a(INSTRUCTION[31:26]), .b(6'b101011), .eq(SW));  // open: gt, lt
  and and_12 (AND, _00_0000, comparator_22_eq);
  and and_13 (SLT, _00_0000, comparator_23_eq);
  and and_14 (NOP, _00_0000, comparator_24_eq);
  and and_15 (HALT, _11_1111, comparator_25_eq);
  and and_16 (RND, _11_1111, comparator_26_eq);
  Comparator #(.width(6)) comparator_28 (.a(INSTRUCTION[31:26]), .b(6'b001101), .eq(ORI));  // open: gt, lt
  Comparator #(.width(6)) comparator_29 (.a(INSTRUCTION[31:26]), .b(6'b000100), .eq(BEQ));  // open: gt, lt
  Comparator #(.width(6)) comparator_30 (.a(INSTRUCTION[31:26]), .b(6'b000001), .eq(BLTZ));  // open: gt, lt
  Comparator #(.width(6)) comparator_31 (.a(INSTRUCTION[5:0]), .b(6'b011001), .eq(comparator_31_eq));  // open: gt, lt
  Comparator #(.width(6)) comparator_32 (.a(INSTRUCTION[5:0]), .b(6'b100101), .eq(comparator_32_eq));  // open: gt, lt
  Comparator #(.width(6)) comparator_33 (.a(INSTRUCTION[5:0]), .b(6'b101010), .eq(comparator_33_eq));  // open: gt, lt
  Comparator #(.width(6)) comparator_34 (.a(INSTRUCTION[5:0]), .b(6'b001000), .eq(comparator_34_eq));  // open: gt, lt
  Comparator #(.width(6)) comparator_35 (.a(INSTRUCTION[5:0]), .b(6'b000001), .eq(comparator_35_eq));  // open: gt, lt
  Comparator #(.width(6)) comparator_36 (.a(INSTRUCTION[5:0]), .b(6'b000100), .eq(comparator_36_eq));  // open: gt, lt
  and and_17 (MULU, _00_0000, comparator_31_eq);
  and and_18 (OR, _00_0000, comparator_32_eq);
  and and_19 (SLTU, _00_0000, comparator_33_eq);
  and and_20 (JR, _00_0000, comparator_34_eq);
  and and_21 (TTY, _11_1111, comparator_35_eq);
  and and_22 (KBD, _11_1111, comparator_36_eq);
  or or_1 (or_1_out, ADDI, ANDI, ORI, XORI);
  or or_2 (or_2_out, SLTI, SLTIU, BEQ, BNE);
  or or_3 (or_3_out, BLEZ, BGTZ, BLTZ, LW, SW);
  Comparator #(.width(6)) comparator_37 (.a(INSTRUCTION[31:26]), .b(6'b001110), .eq(XORI));  // open: gt, lt
  Comparator #(.width(6)) comparator_38 (.a(INSTRUCTION[31:26]), .b(6'b000101), .eq(BNE));  // open: gt, lt
  Comparator #(.width(6)) comparator_39 (.a(INSTRUCTION[31:26]), .b(6'b100011), .eq(LW));  // open: gt, lt
  or or_4 (TYPE_I, or_1_out, or_2_out, or_3_out);

  assign CONSTANTE = INSTRUCTION[15:0];
  assign DESTINO_SALTO = INSTRUCTION[25:0];
  assign RD = INSTRUCTION[15:11];
  assign RS = INSTRUCTION[25:21];
  assign RT = INSTRUCTION[20:16];

  // Other names for the same wires on the sheet: FUNC_CODE[5:0] = INSTRUCTION[5:0]; OP_CODE[5:0] = INSTRUCTION[31:26]

  // Notes on the sheet:
  //   OP_CODE:00 0000
  //   INPUTS
  //   TYPE_J_CODE
  //   TYPE_R_CODE
  //   11 1000
  //   TYPE_R
  //   OP_CODE:11 1000
  //   INSTRUCTIONS
  //   00 0000
  //   OP_CODE:11 1111
  //   OUTPUTS
  //   TYPE_I_CODE
  //   11 1111
  //   TYPE_I
  //   TYPE_J
endmodule

module Sign_Extend (
  input  [15:0] _16_Bit_Input,
  output [31:0] _32_Bit_Output
);

  Multiplexer #(.width(17)) multiplexer_1 (
    .in0({17{1'b0}}), .in1({17{1'b1}}), .out(_32_Bit_Output[31:15]), .sel(_16_Bit_Input[15]));  // open: en

  assign _32_Bit_Output[14:0] = _16_Bit_Input[14:0];
endmodule

module Branch_Control (
  input  [31:0] PC,
  input  [31:0] RS,
  input  [25:0] DESTINO_SALTO,
  input  [15:0] CONSTANTE,
  input  NOP,
  input  BGTZ,
  input  BEQ,
  input  BLTZ,
  input  BNE,
  input  J,
  input  BLEZ,
  input  JR,
  input  RS_____RT,
  input  RS____0,
  input  RS____0_2,
  output [31:0] PC_2
);

  wire _01, and_1_out, and_2_out, and_3_out, and_4_out, and_5_out, FLAG, priority_encoder_1_en_out;
  wire [1:0] priority_encoder_1_out, SELECTOR_BC;
  wire [31:0] PC___4, PC___4___4___OFFSET, SALTO_CONDICIONAL;
  wire [31:18] _4___OFFSET;

  Adder #(.width(32)) adder_1 (.a(PC), .b(32'h4), .out(PC___4));  // open: cin, cout
  assign _4___OFFSET = {{13{CONSTANTE[15]}}, CONSTANTE[15]};  // Bit_Extender bit_extender_1
  Adder #(.width(32)) adder_2 (
    .a(PC___4), .b({_4___OFFSET, CONSTANTE, 2'b00}), .out(PC___4___4___OFFSET));  // open: cin, cout
  Priority_Encoder #(.select(2)) priority_encoder_1 (
    .in0(NOP), .in1(_01), .in2(J), .in3(JR), .out(priority_encoder_1_out), .en_out(priority_encoder_1_en_out));  // open: gs, en_in
  and and_1 (and_1_out, BEQ, RS_____RT);
  and and_2 (and_2_out, ~RS_____RT, BNE);  // AND_Gate
  and and_3 (and_3_out, BLEZ, RS____0);
  and and_4 (and_4_out, ~RS____0, BGTZ);  // AND_Gate
  and and_5 (and_5_out, BLTZ, RS____0_2);
  or or_1 (_01, BEQ, BNE, BLEZ, BGTZ, BLTZ);
  Multiplexer #(.width(2), .enable("false")) multiplexer_1 (
    .in0(priority_encoder_1_out), .in1(2'b00), .out(SELECTOR_BC), .sel(priority_encoder_1_en_out));
  or or_2 (FLAG, and_1_out, and_2_out, and_3_out, and_4_out, and_5_out);
  Multiplexer #(.width(32), .enable("false")) multiplexer_2 (
    .in0(PC___4), .in1(PC___4___4___OFFSET), .out(SALTO_CONDICIONAL), .sel(FLAG));
  Multiplexer #(.select(2), .width(32), .enable("false")) multiplexer_3 (
    .in0(PC___4), .in1(SALTO_CONDICIONAL), .in2(RS), .in3({PC[31:28], DESTINO_SALTO, 2'b00}), .out(PC_2),
    .sel(SELECTOR_BC));

  // Other names for the same wires on the sheet: _4___OFFSET[17:2] = CONSTANTE; PC_OUT[31:0] = PC_2;
  //   REGISTRO[31:0] = RS; RS____0_t = RS____0_2; SALTO[31:2] = {PC[31:28], DESTINO_SALTO}

  // Notes on the sheet:
  //   INPUTS
  //   INSTRUCTIONS
  //   FLAGS
  //   OUTPUTS
endmodule

module Sign_Multiplier (
  input  [31:0] OP_1,
  input  [31:0] OP_2,
  output [31:0] LOW,
  output [31:0] HIGH
);

  wire CARRY, NEG, NEG_1, NEG_2;
  wire [31:0] adder_1_out, adder_2_out, bit_negator_1_opposite, bit_negator_2_opposite, multiplexer_1_out,
       multiplexer_2_out, multiplier_1_cout, multiplier_1_out, negator_1_out, negator_2_out;

  // Probe on OP_1
  // Probe on OP_2
  Negator #(.width(32)) negator_1 (.in(OP_1), .out(negator_1_out));
  Negator #(.width(32)) negator_2 (.in(OP_2), .out(negator_2_out));
  Comparator #(.width(1)) comparator_1 (.a(OP_2[31]), .b(1'b1), .eq(NEG_2));  // open: gt, lt
  Comparator #(.width(1)) comparator_2 (.a(1'b1), .b(OP_1[31]), .eq(NEG_1));  // open: gt, lt
  Multiplexer #(.width(32), .enable("false")) multiplexer_1 (
    .in0(OP_1), .in1(negator_1_out), .out(multiplexer_1_out), .sel(NEG_1));
  Multiplexer #(.width(32), .enable("false")) multiplexer_2 (
    .in0(OP_2), .in1(negator_2_out), .out(multiplexer_2_out), .sel(NEG_2));
  Multiplier #(.width(32)) multiplier_1 (
    .a(multiplexer_1_out), .b(multiplexer_2_out), .out(multiplier_1_out), .cout(multiplier_1_cout));  // open: cin
  Bit_Negator bit_negator_1 (.NUMBER(multiplier_1_out), .OPPOSITE(bit_negator_1_opposite));
  Bit_Negator bit_negator_2 (.NUMBER(multiplier_1_cout), .OPPOSITE(bit_negator_2_opposite));
  xor xor_1 (NEG, NEG_1, NEG_2);
  Adder #(.width(32)) adder_1 (.a(bit_negator_1_opposite), .b(32'h1), .out(adder_1_out), .cout(CARRY));  // open: cin
  Adder #(.width(32)) adder_2 (
    .a(bit_negator_2_opposite), .b({32{1'b0}}), .out(adder_2_out), .cin(CARRY));  // open: cout
  Multiplexer #(.width(32), .enable("false")) multiplexer_3 (
    .in0(multiplier_1_out), .in1(adder_1_out), .out(LOW), .sel(NEG));
  Multiplexer #(.width(32), .enable("false")) multiplexer_4 (
    .in0(multiplier_1_cout), .in1(adder_2_out), .out(HIGH), .sel(NEG));
  // Probe on LOW
  // Probe on HIGH

  // Notes on the sheet:
  //   INPUTS
  //   SIGNS
  //   OUTPUTS
endmodule

module Sign_Divider (
  input  [31:0] DIVIDEND,
  input  [31:0] DIVISOR,
  output [31:0] LOW,
  output [31:0] HIGH
);

  wire DIVIDEND_SIGN, DIVISOR_SIGN, REST_IS_ZERO;
  wire [31:0] minus_NEGATIVE_QUOTIENT, minus_POSITIVE_QUOTIENT, multiplexer_1_out, multiplexer_2_out,
       NEGATIVE_QUOTIENT, negator_3_out, negator_4_out, POSITIVE_QUOTIENT, QUOTIENT_INCREASE, REST,
       sign_multiplier_1_low;

  // Probe on DIVIDEND
  // Probe on DIVISOR
  Negator #(.width(32)) negator_1 (.in(POSITIVE_QUOTIENT), .out(minus_POSITIVE_QUOTIENT));
  Adder #(.width(32)) adder_1 (
    .a(POSITIVE_QUOTIENT), .b(QUOTIENT_INCREASE), .out(NEGATIVE_QUOTIENT));  // open: cin, cout
  Negator #(.width(32)) negator_2 (.in(NEGATIVE_QUOTIENT), .out(minus_NEGATIVE_QUOTIENT));
  Negator #(.width(32)) negator_3 (.in(DIVIDEND), .out(negator_3_out));
  Negator #(.width(32)) negator_4 (.in(DIVISOR), .out(negator_4_out));
  Comparator #(.width(1)) comparator_1 (.a(DIVISOR[31]), .b(1'b1), .eq(DIVISOR_SIGN));  // open: gt, lt
  Comparator #(.width(1)) comparator_2 (.a(1'b1), .b(DIVIDEND[31]), .eq(DIVIDEND_SIGN));  // open: gt, lt
  Multiplexer #(.width(32), .enable("false")) multiplexer_1 (
    .in0(DIVIDEND), .in1(negator_3_out), .out(multiplexer_1_out), .sel(DIVIDEND_SIGN));
  Multiplexer #(.width(32), .enable("false")) multiplexer_2 (
    .in0(DIVISOR), .in1(negator_4_out), .out(multiplexer_2_out), .sel(DIVISOR_SIGN));
  // Probe on POSITIVE_QUOTIENT
  Divider #(.width(32)) divider_1 (
    .a(multiplexer_1_out), .b(multiplexer_2_out), .out(POSITIVE_QUOTIENT), .rem(REST));  // open: upper
  // Probe on REST
  Comparator #(.width(32)) comparator_3 (.a({32{1'b0}}), .b(REST), .eq(REST_IS_ZERO));  // open: gt, lt
  Multiplexer #(.width(32), .enable("false")) multiplexer_3 (
    .in0(32'h1), .in1({32{1'b0}}), .out(QUOTIENT_INCREASE), .sel(REST_IS_ZERO));
  Sign_Multiplier sign_multiplier_1 (.OP_1(DIVISOR), .OP_2(LOW), .LOW(sign_multiplier_1_low));  // open: HIGH
  Multiplexer #(.select(2), .width(32), .enable("false")) multiplexer_4 (
    .in0(POSITIVE_QUOTIENT), .in1(minus_POSITIVE_QUOTIENT), .in2(minus_NEGATIVE_QUOTIENT),
    .in3(NEGATIVE_QUOTIENT), .out(LOW), .sel({DIVIDEND_SIGN, DIVISOR_SIGN}));
  Subtractor #(.width(32)) subtractor_1 (.a(DIVIDEND), .b(sign_multiplier_1_low), .out(HIGH));  // open: bin, bout
  // Probe on HIGH
  // Probe on LOW

  // Other names for the same wires on the sheet: QUOTIENT[31:0] = LOW;
  //   QUOTIENT_SIGN[1:0] = {DIVIDEND_SIGN, DIVISOR_SIGN}

  // Notes on the sheet:
  //   INPUTS
  //   QUOTIENT_SIGN
  //   OUTPUTS
endmodule

module Bit_Negator (
  input  [31:0] NUMBER,
  output [31:0] OPPOSITE
);

  wire [31:0] negator_1_out;

  // Probe on NUMBER
  // Probe on negator_1_out
  Negator #(.width(32)) negator_1 (.in(NUMBER), .out(negator_1_out));
  Subtractor #(.width(32)) subtractor_1 (.a(negator_1_out), .b(32'h1), .out(OPPOSITE));  // open: bin, bout
  // Probe on OPPOSITE

  // Notes on the sheet:
  //   INPUTS
  //   OUTPUTS
endmodule

module RAM_Instructions (
  input  [31:0] ALU,
  input  [31:0] SP,
  input  [31:0] PC,
  input  LW,
  input  SW,
  input  POP,
  input  PUSH,
  input  PC_INST,
  output [31:0] DIR_RAM
);

  wire [1:0] RAM_SELECT;
  wire [31:0] multiplexer_1_out, SP___4;

  Subtractor #(.width(32)) subtractor_1 (.a(SP), .b(32'h4), .out(SP___4));  // open: bin, bout
  or or_1 (RAM_SELECT[0], LW, SW, PC_INST);
  or or_2 (RAM_SELECT[1], PC_INST, POP, PUSH);
  Multiplexer #(.width(32), .enable("false")) multiplexer_1 (
    .in0(SP), .in1(SP___4), .out(multiplexer_1_out), .sel(PUSH));
  Multiplexer #(.select(2), .width(32), .enable("false")) multiplexer_2 (
    .in0(PC), .in1(ALU), .in2(multiplexer_1_out), .in3(PC), .out(DIR_RAM), .sel(RAM_SELECT));

  // Notes on the sheet:
  //   INPUTS
  //   OUTPUTS
endmodule
