// Logisim project Para_Trabajar.circ as structural Verilog
module S_MIPS_Board (
  input  DESHABILITAR_DISPATCHER,
  output halt
);

  wire button_1_out, CLK, CS, d_ff_1_q, LCLR, LoadRAM, LoadRAMOn, LW, R_R_W, R_W, ram_dispatcher_1_finished,
       RCS, Reset_out, RST, TTY_EN;
  wire [2:0] KDB;
  wire [3:0] LMask, Mask, ram_1_read_time, ram_1_write_time, RMask;
  wire [6:0] KDB_DATA, TTY_DATA;
  wire [15:0] Addr, LAddr, RAddr;
  wire [31:0] I0, I1, I2, I3, LData, ram_1_data_out_0, ram_1_data_out_1, ram_1_data_out_2, ram_1_data_out_3,
       RI0, RI1, RI2, RI3;

  TTY #(.rows(25), .cols(80)) tty_1 (.clk(CLK), .we(TTY_EN), .clr(RST));  // open: data
  not not_1 (LoadRAMOn, ram_dispatcher_1_finished);
  s_mips_RAM_Dispatcher ram_dispatcher_1 (
    .WriteTime(ram_1_write_time), .Clock(CLK), .Data(LData), .Address(LAddr), .Mask(LMask),
    .Finished(ram_dispatcher_1_finished), .Write(LW), .CLR(LCLR));
  Keyboard #(.buflen(64)) keyboard_1 (.clk(CLK), .re(KDB[0]), .avail(KDB[2]), .data(KDB_DATA));  // open: clr
  s_mips_RAM ram_1 (
    .Address(RAddr), .Data_Out_0(ram_1_data_out_0), .Data_Out_1(ram_1_data_out_1),
    .Data_Out_2(ram_1_data_out_2), .Data_Out_3(ram_1_data_out_3), .Data_In_0(RI0), .Data_In_1(RI1),
    .Data_In_2(RI2), .Data_In_3(RI3), .Mask(RMask), .nRead_Write(R_R_W), .Chip_Select(RCS),
    .Read_Time(ram_1_read_time), .Reset(button_1_out), .Write_Time(ram_1_write_time));
  Button button_1 (.out(button_1_out));
  D_Flip_Flop d_ff_1 (.clk(CLK), .D(1'b1), .Q(d_ff_1_q), .reset(Reset_out));  // open: Qn, preset, en
  Button Reset (.out(Reset_out));
  s_mips_S_MIPS s_mips_1 (
    .Kbd_Enable(KDB[0]), .Address(Addr), .Kbd_Clear(KDB[1]), .Kbd_Available(KDB[2]), .RAM_In_0(I0),
    .Kbd_ASCII_Data(KDB_DATA), .RAM_In_1(I1), .TTY_Enable(TTY_EN), .RAM_In_2(I2), .RAM_In_3(I3),
    .TTY_ASCII_Data(TTY_DATA), .Reset(RST), .RAM_Out_0(ram_1_data_out_0), .Clock(CLK),
    .RAM_Out_1(ram_1_data_out_1), .Stop(halt), .RAM_Out_2(ram_1_data_out_2), .RAM_Out_3(ram_1_data_out_3),
    .Mask(Mask), .Read_Time(ram_1_read_time), .Write_Time(ram_1_write_time), .nRead_Write(R_W),
    .Chip_Select(CS));
  D_Flip_Flop d_ff_2 (.clk(CLK), .D(d_ff_1_q), .Qn(LCLR), .reset(Reset_out));  // open: Q, preset, en
  or or_1 (RST, LCLR, LoadRAM);
  Clock clock_1 (.out(CLK));
  Multiplexer #(.width(32), .enable("false")) multiplexer_1 (.in0(I0), .in1(LData), .out(RI0), .sel(LoadRAM));
  Multiplexer #(.width(32), .enable("false")) multiplexer_2 (.in0(I1), .in1(LData), .out(RI1), .sel(LoadRAM));
  Multiplexer #(.width(32), .enable("false")) multiplexer_3 (.in0(I2), .in1(LData), .out(RI2), .sel(LoadRAM));
  Multiplexer #(.width(32), .enable("false")) multiplexer_4 (.in0(I3), .in1(LData), .out(RI3), .sel(LoadRAM));
  and and_1 (LoadRAM, ~DESHABILITAR_DISPATCHER, LoadRAMOn);  // AND_Gate
  Multiplexer #(.width(16), .enable("false")) multiplexer_5 (.in0(Addr), .in1(LAddr), .out(RAddr), .sel(LoadRAM));
  Multiplexer #(.width(4), .enable("false")) multiplexer_6 (.in0(Mask), .in1(LMask), .out(RMask), .sel(LoadRAM));
  Multiplexer #(.enable("false")) multiplexer_7 (.in0(CS), .in1(LW), .out(RCS), .sel(LoadRAM));
  Multiplexer #(.enable("false")) multiplexer_8 (.in0(R_W), .in1(LW), .out(R_R_W), .sel(LoadRAM));

  // Notes on the sheet:
  //   Keyboard
endmodule

module RAM (
  input  [31:0] Data_In_0,
  input  [31:0] Data_In_1,
  input  [31:0] Data_In_2,
  input  [31:0] Data_In_3,
  input  [3:0] Mask,
  input  nRead_Write,
  input  Chip_Select,
  input  Reset,
  output [31:0] Data_Out_0,
  output [31:0] Data_Out_1,
  output [31:0] Data_Out_2,
  output [31:0] Data_Out_3,
  output [3:0] Read_Time,
  output [3:0] Write_Time
);

  wire and_2_out, and_3_out, and_4_out, and_5_out, and_6_out, and_7_out, and_8_out, and_9_out, Changed, CLK,
       comparator_2_eq, comparator_3_eq, comparator_4_eq, comparator_5_eq, comparator_6_eq, Count,
       demultiplexer_3_out0, Idle, Idle_q, Load, Load0, Load1, nand_1_out, or_1_out, or_2_out, or_3_out,
       or_4_out, or_5_out, or_6_out, or_7_out, or_8_out, or_9_out, or_10_out, Proc_q, Update_Mem, Zero_Time;
  wire [3:0] counter_1_q, multiplexer_1_out, subtractor_1_out;
  wire [15:0] Address;
  wire [31:0] register_1_q, register_2_q, register_3_q, register_4_q, register_5_q;

  // Probe on 4'b0011
  // Probe on 4'b0010
  Multiplexer #(.width(4), .enable("false")) multiplexer_1 (
    .in0(4'b0011), .in1(4'b0010), .out(multiplexer_1_out), .sel(nRead_Write));
  or or_1 (or_1_out, Idle, Update_Mem);
  or or_2 (or_2_out, ~Chip_Select, Reset);  // OR_Gate
  Subtractor #(.width(4)) subtractor_1 (.a(multiplexer_1_out), .b(4'b0010), .out(subtractor_1_out));  // open: bin, bout
  D_Flip_Flop u_Idle (.clk(CLK), .D(or_1_out), .Q(Idle_q), .preset(or_2_out));  // open: Qn, en, reset
  Demultiplexer #(.enable("false")) demultiplexer_1 (.out0(Idle), .out1(Load0), .in(Idle_q), .sel(Changed));
  Counter #(.width(4), .max('hf)) counter_1 (
    .load(Load), .D(subtractor_1_out), .count(Count), .Q(counter_1_q), .clk(CLK), .clr(or_3_out));  // open: carry
  or or_3 (or_3_out, ~Chip_Select, Reset);  // OR_Gate
  Comparator #(.width(4), .mode("unsigned")) comparator_1 (
    .a(4'b0000), .b(counter_1_q), .eq(Zero_Time));  // open: gt, lt
  or or_4 (or_4_out, Count, Load0, Load1);
  Register #(.width(32)) register_1 (.D(Data_In_0), .en(Chip_Select), .Q(register_1_q), .clk(CLK), .clr(or_5_out));
  or or_5 (or_5_out, ~Chip_Select, Reset);  // OR_Gate
  Register #(.width(32)) register_2 (.D(Data_In_1), .en(Chip_Select), .Q(register_2_q), .clk(CLK), .clr(or_6_out));
  or or_6 (or_6_out, ~Chip_Select, Reset);  // OR_Gate
  Register #(.width(32)) register_3 (.D(Data_In_2), .en(Chip_Select), .Q(register_3_q), .clk(CLK), .clr(or_7_out));
  or or_7 (or_7_out, ~Chip_Select, Reset);  // OR_Gate
  Register #(.width(32)) register_4 (.D(Data_In_3), .en(Chip_Select), .Q(register_4_q), .clk(CLK), .clr(or_8_out));
  or or_8 (or_8_out, ~Chip_Select, Reset);  // OR_Gate
  Register #(.width(32)) register_5 (
    .D({{11{1'b1}}, nRead_Write, Mask, Address}), .en(Chip_Select), .Q(register_5_q), .clk(CLK),
    .clr(or_9_out));
  or or_9 (or_9_out, ~Chip_Select, Reset);  // OR_Gate
  D_Flip_Flop Proc (.clk(CLK), .D(or_4_out), .Q(Proc_q), .reset(or_10_out));  // open: Qn, preset, en
  or or_10 (or_10_out, ~Chip_Select, Reset);  // OR_Gate
  Demultiplexer #(.enable("false")) demultiplexer_2 (
    .out0(Count), .out1(Update_Mem), .in(demultiplexer_3_out0), .sel(Zero_Time));
  Demultiplexer #(.enable("false")) demultiplexer_3 (
    .out0(demultiplexer_3_out0), .out1(Load1), .in(Proc_q), .sel(Changed));
  Clock clock_1 (.out(CLK));
  Comparator #(.width(32)) comparator_2 (.a(register_1_q), .b(Data_In_0), .eq(comparator_2_eq));  // open: gt, lt
  Comparator #(.width(32)) comparator_3 (.a(register_2_q), .b(Data_In_1), .eq(comparator_3_eq));  // open: gt, lt
  Comparator #(.width(32)) comparator_4 (.a(register_3_q), .b(Data_In_2), .eq(comparator_4_eq));  // open: gt, lt
  Comparator #(.width(32)) comparator_5 (.a(register_4_q), .b(Data_In_3), .eq(comparator_5_eq));  // open: gt, lt
  Comparator #(.width(32)) comparator_6 (
    .a(register_5_q), .b({{11{1'b1}}, nRead_Write, Mask, Address}), .eq(comparator_6_eq));  // open: gt, lt
  nand nand_1 (nand_1_out, comparator_6_eq, comparator_2_eq, comparator_3_eq, comparator_4_eq, comparator_5_eq);
  and and_1 (Changed, nand_1_out, Chip_Select);
  or or_11 (Load, Count, Load1, Load0);
  and and_2 (and_2_out, Mask[0], Update_Mem, nRead_Write);
  and and_3 (and_3_out, Mask[1], Update_Mem, nRead_Write);
  and and_4 (and_4_out, Mask[2], Update_Mem, nRead_Write);
  and and_5 (and_5_out, Mask[3], Update_Mem, nRead_Write);
  RAM_part #(.addrWidth(16), .dataWidth(32), .bus("separate")) ram_1 (
    .addr(Address), .din(Data_In_0), .data(Data_Out_0), .str(and_2_out), .sel(Chip_Select), .clk(CLK),
    .ld(and_6_out), .clr(Reset));
  and and_6 (and_6_out, ~nRead_Write, Idle);  // AND_Gate
  RAM_part #(.addrWidth(16), .dataWidth(32), .bus("separate")) ram_2 (
    .addr(Address), .din(Data_In_1), .data(Data_Out_1), .str(and_3_out), .sel(Chip_Select), .clk(CLK),
    .ld(and_7_out), .clr(Reset));
  and and_7 (and_7_out, ~nRead_Write, Idle);  // AND_Gate
  RAM_part #(.addrWidth(16), .dataWidth(32), .bus("separate")) ram_3 (
    .addr(Address), .din(Data_In_2), .data(Data_Out_2), .str(and_4_out), .sel(Chip_Select), .clk(CLK),
    .ld(and_8_out), .clr(Reset));
  and and_8 (and_8_out, ~nRead_Write, Idle);  // AND_Gate
  RAM_part #(.addrWidth(16), .dataWidth(32), .bus("separate")) ram_4 (
    .addr(Address), .din(Data_In_3), .data(Data_Out_3), .str(and_5_out), .sel(Chip_Select), .clk(CLK),
    .ld(and_9_out), .clr(Reset));
  and and_9 (and_9_out, ~nRead_Write, Idle);  // AND_Gate

  assign Read_Time = 4'b0011;
  assign Write_Time = 4'b0010;

  // Other names for the same wires on the sheet: M0 = Mask[0]; M1 = Mask[1]; M2 = Mask[2]; M3 = Mask[3];
  //   RW = nRead_Write; CLR = Reset; CS = Chip_Select; Load2 = Count

  // Notes on the sheet:
  //   NO MODIFICAR
  //   excepto quizás los valores RT y WT
  //   BANK0
  //   BANK1
  //   BANK2
  //   BANK3
endmodule

module S_MIPS (
  input  Kbd_Available,
  input  [6:0] Kbd_ASCII_Data,
  input  [31:0] RAM_Out_0,
  input  [31:0] RAM_Out_1,
  input  Reset,
  input  [31:0] RAM_Out_2,
  input  Clock,
  input  [31:0] RAM_Out_3,
  input  [3:0] Read_Time,
  input  [3:0] Write_Time,
  output Kbd_Enable,
  output [15:0] Address,
  output Kbd_Clear,
  output TTY_Enable,
  output [6:0] TTY_ASCII_Data,
  output Stop,
  output [31:0] RAM_In_0,
  output [31:0] RAM_In_1,
  output [31:0] RAM_In_2,
  output [31:0] RAM_In_3,
  output [3:0] Mask,
  output nRead_Write,
  output Chip_Select
);


  // Other names for the same wires on the sheet: CLK = Clock; CLR = Reset; CS = Chip_Select;
  //   KBD_AVAIL = Kbd_Available; KBD_CLR = Kbd_Clear; KBD_DATA[6:0] = Kbd_ASCII_Data; RAM_A[15:0] = Address;
  //   RAM_INPUT_0[31:0] = RAM_In_0; RAM_INPUT_1[31:0] = RAM_In_1; RAM_INPUT_2[31:0] = RAM_In_2;
  //   RAM_INPUT_3[31:0] = RAM_In_3; RAM_MASK[3:0] = Mask; RAM_OUTPUT_0[31:0] = RAM_Out_0;
  //   RAM_OUTPUT_1[31:0] = RAM_Out_1; RAM_OUTPUT_2[31:0] = RAM_Out_2; RAM_OUTPUT_3[31:0] = RAM_Out_3;
  //   RW = nRead_Write; TTY_DATA[6:0] = TTY_ASCII_Data

  // Notes on the sheet:
  //   RAM ADDRESS
  //   DATA FROM RAM
  //   DATA TO RAM
  //   DATA WRITE MASK
  //   RAM TIMING
  //   RAM CONTROL
  //   KEYBOARD
  //   TTY
  //   SEQUENCING
endmodule

module RAM_Dispatcher (
  input  [3:0] WriteTime,
  input  Clock,
  input  CLR,
  output [31:0] Data,
  output [15:0] Address,
  output [3:0] Mask,
  output Finished,
  output Write
);

  wire demultiplexer_2_out1, demultiplexer_3_out1, End, IDLE_q, IncAddr, Load, or_1_out, or_2_out, While_q,
       WriteEnd;
  wire [3:0] counter_1_q;
  wire [31:0] CurrentAddress_q;

  Counter #(.width(32), .max('hffffffff)) CurrentAddress (
    .count(IncAddr), .Q({CurrentAddress_q[31:18], Address, CurrentAddress_q[1:0]}), .clk(Clock), .clr(CLR));  // open: load, D, carry
  or or_1 (or_1_out, IncAddr, demultiplexer_3_out1, Finished);
  D_Flip_Flop IDLE (.clk(Clock), .D(or_1_out), .Q(IDLE_q), .preset(CLR));  // open: Qn, en, reset
  Demultiplexer #(.enable("false")) demultiplexer_1 (.out0(Load), .out1(Finished), .in(IDLE_q), .sel(End));
  D_Flip_Flop While (.clk(Clock), .D(or_2_out), .Q(While_q), .reset(CLR));  // open: Qn, preset, en
  or or_2 (or_2_out, Write, Load);
  RAM_part #(.addrWidth(18), .dataWidth(32)) ram_1 (
    .addr({Address, CurrentAddress_q[1:0]}), .data(Data), .clk(Clock));  // open: sel, ld, clr
  Demultiplexer #(.enable("false")) demultiplexer_2 (
    .out0(Write), .out1(demultiplexer_2_out1), .in(While_q), .sel(WriteEnd));
  Decoder #(.select(2)) decoder_1 (
    .out0(Mask[0]), .out1(Mask[1]), .out2(Mask[2]), .out3(Mask[3]), .sel(CurrentAddress_q[1:0]));  // open: en
  Demultiplexer #(.enable("false")) demultiplexer_3 (
    .out0(IncAddr), .out1(demultiplexer_3_out1), .in(demultiplexer_2_out1), .sel(End));
  Counter #(.width(4), .max('hf)) counter_1 (
    .load(Load), .D(WriteTime), .count(Write), .Q(counter_1_q), .clk(Clock));  // open: carry, clr
  Comparator #(.width(32)) comparator_1 (.a(Data), .b({32{1'b1}}), .eq(End));  // open: gt, lt
  Comparator #(.width(4)) comparator_2 (.a(4'b0000), .b(counter_1_q), .eq(WriteEnd));  // open: gt, lt

  // Other names for the same wires on the sheet: CLK = Clock; Count = Write; WT[3:0] = WriteTime
endmodule

module Program_Counter_2 (
  input  [31:0] Branch_Control,
  input  Reset,
  input  Enabled,
  input  Clock,
  output [31:0] Instruction
);

  Register #(.width(32)) PC (.D(Branch_Control), .en(Enabled), .Q(Instruction), .clk(Clock), .clr(Reset));
endmodule

module Register_File_2 (
  input  [4:0] RW,
  input  [31:0] DATA_IN,
  input  W_E,
  input  [4:0] R1_ADDRESS,
  input  [4:0] R2_ADDRESS,
  input  CLK,
  input  RST,
  input  [31:0] HIGH_INPUT,
  input  HIGH_LOW_ENABLE,
  input  PUSH,
  input  POP,
  input  PROGRAM_COUNTER_ENABLE,
  output [31:0] R1_OUTPUT,
  output [31:0] R2_OUTPUT,
  output [31:0] HIGH,
  output [31:0] LOW,
  output [31:0] STACK_POINTER
);

  wire BANK0_SELECT, BANK1_SELECT, BANK2_SELECT, BANK3_SELECT, R1_WRITE, R2_WRITE, R3_WRITE, R4_WRITE,
       R5_WRITE, R6_WRITE, R7_WRITE, R8_WRITE, R9_WRITE, R10_WRITE, R11_WRITE, R12_WRITE, R13_WRITE,
       R14_WRITE, R15_WRITE, R16_WRITE, R17_WRITE, R18_WRITE, R19_WRITE, R20_WRITE, R21_WRITE, R22_WRITE,
       R23_WRITE, R24_WRITE, R25_WRITE, R26_WRITE, R27_WRITE, R28_WRITE, R29_WRITE, R30_WRITE, R31_WRITE;
  wire [31:0] multiplexer_1_out, multiplexer_2_out, multiplexer_3_out, multiplexer_4_out, multiplexer_6_out,
       multiplexer_7_out, multiplexer_8_out, multiplexer_9_out, R0, R1, R2, R3, R4, R5, R6, R7, R8, R9, R10,
       R11, R12, R13, R14, R15, R16, R17, R18, R19, R20, R21, R22, R23, R24, R25, R26, R27, R28, R29, R30,
       undriven, undriven_2, undriven_3;

  Register #(.width(32)) zero (.D({32{1'b0}}), .Q(R0), .clk(CLK), .clr(RST));  // open: en
  Register #(.width(32)) t0 (.D(DATA_IN), .en(R8_WRITE), .Q(R8), .clk(CLK), .clr(RST));
  Register #(.width(32)) s0 (.D(DATA_IN), .en(R16_WRITE), .Q(R16), .clk(CLK), .clr(RST));
  Register #(.width(32)) t8 (.D(DATA_IN), .en(R24_WRITE), .Q(R24), .clk(CLK), .clr(RST));
  Multiplexer #(.select(3), .width(32), .disabled(0), .enable("false")) multiplexer_1 (
    .in0(R0), .in1(R1), .in2(R2), .in3(R3), .in4(R4), .in5(R5), .in6(R6), .in7(R7), .out(multiplexer_1_out),
    .sel(R1_ADDRESS[2:0]));
  Multiplexer #(.select(3), .width(32), .disabled(0), .enable("false")) multiplexer_2 (
    .in0(R8), .in1(R9), .in2(R10), .in3(R11), .in4(R12), .in5(R13), .in6(R14), .in7(R15),
    .out(multiplexer_2_out), .sel(R1_ADDRESS[2:0]));
  Multiplexer #(.select(3), .width(32), .disabled(0), .enable("false")) multiplexer_3 (
    .in0(R16), .in1(R17), .in2(R18), .in3(R19), .in4(R20), .in5(R21), .in6(R22), .in7(R23),
    .out(multiplexer_3_out), .sel(R1_ADDRESS[2:0]));
  Multiplexer #(.select(3), .width(32), .disabled(0), .enable("false")) multiplexer_4 (
    .in0(R24), .in1(R25), .in2(R26), .in3(R27), .in4(R28), .in5(R29), .in6(R30), .in7(STACK_POINTER),
    .out(multiplexer_4_out), .sel(R1_ADDRESS[2:0]));
  Register #(.width(32)) at (.D(DATA_IN), .en(R1_WRITE), .Q(R1), .clk(CLK), .clr(RST));
  Register #(.width(32)) t1 (.D(DATA_IN), .en(R9_WRITE), .Q(R9), .clk(CLK), .clr(RST));
  Register #(.width(32)) s1 (.D(DATA_IN), .en(R17_WRITE), .Q(R17), .clk(CLK), .clr(RST));
  Register #(.width(32)) t9 (.D(DATA_IN), .en(R25_WRITE), .Q(R25), .clk(CLK), .clr(RST));
  Demultiplexer #(.select(3), .disabled(0)) demultiplexer_1 (
    .out1(R1_WRITE), .out2(R2_WRITE), .out3(R3_WRITE), .out4(R4_WRITE), .out5(R5_WRITE), .out6(R6_WRITE),
    .out7(R7_WRITE), .in(1'b1), .sel(RW[2:0]), .en(BANK0_SELECT));  // open: out0
  Demultiplexer #(.select(3), .disabled(0)) demultiplexer_2 (
    .out0(R16_WRITE), .out1(R17_WRITE), .out2(R18_WRITE), .out3(R19_WRITE), .out4(R20_WRITE),
    .out5(R21_WRITE), .out6(R22_WRITE), .out7(R23_WRITE), .in(1'b1), .sel(RW[2:0]), .en(BANK2_SELECT));
  Multiplexer #(.select(2), .width(32), .enable("false")) multiplexer_5 (
    .in0(multiplexer_1_out), .in1(multiplexer_2_out), .in2(multiplexer_3_out), .in3(multiplexer_4_out),
    .out(R1_OUTPUT), .sel(R1_ADDRESS[4:3]));
  Demultiplexer #(.select(2), .disabled(0)) demultiplexer_3 (
    .out0(BANK0_SELECT), .out1(BANK1_SELECT), .out2(BANK2_SELECT), .out3(BANK3_SELECT), .in(1'b1),
    .sel(RW[4:3]), .en(W_E));
  Register #(.width(32)) v0 (.D(DATA_IN), .en(R2_WRITE), .Q(R2), .clk(CLK), .clr(RST));
  Register #(.width(32)) t2 (.D(DATA_IN), .en(R10_WRITE), .Q(R10), .clk(CLK), .clr(RST));
  Register #(.width(32)) s2 (.D(DATA_IN), .en(R18_WRITE), .Q(R18), .clk(CLK), .clr(RST));
  Register #(.width(32)) t10 (.D(DATA_IN), .en(R26_WRITE), .Q(R26), .clk(CLK), .clr(RST));
  Demultiplexer #(.select(3), .disabled(0)) demultiplexer_4 (
    .out0(R8_WRITE), .out1(R9_WRITE), .out2(R10_WRITE), .out3(R11_WRITE), .out4(R12_WRITE), .out5(R13_WRITE),
    .out6(R14_WRITE), .out7(R15_WRITE), .in(1'b1), .sel(RW[2:0]), .en(BANK1_SELECT));
  Demultiplexer #(.select(3), .disabled(0)) demultiplexer_5 (
    .out0(R24_WRITE), .out1(R25_WRITE), .out2(R26_WRITE), .out3(R27_WRITE), .out4(R28_WRITE),
    .out5(R29_WRITE), .out6(R30_WRITE), .out7(R31_WRITE), .in(1'b1), .sel(RW[2:0]), .en(BANK3_SELECT));
  Register #(.width(32)) v1 (.D(DATA_IN), .en(R3_WRITE), .Q(R3), .clk(CLK), .clr(RST));
  Register #(.width(32)) t3 (.D(DATA_IN), .en(R11_WRITE), .Q(R11), .clk(CLK), .clr(RST));
  Register #(.width(32)) s3 (.D(DATA_IN), .en(R19_WRITE), .Q(R19), .clk(CLK), .clr(RST));
  Register #(.width(32)) t11 (.D(DATA_IN), .en(R27_WRITE), .Q(R27), .clk(CLK), .clr(RST));
  Multiplexer #(.select(3), .width(32), .disabled(0), .enable("false")) multiplexer_6 (
    .in0(R0), .in1(R1), .in2(R2), .in3(R3), .in4(R4), .in5(R5), .in6(R6), .in7(R7), .out(multiplexer_6_out),
    .sel(R2_ADDRESS[2:0]));
  Multiplexer #(.select(3), .width(32), .disabled(0), .enable("false")) multiplexer_7 (
    .in0(R8), .in1(R9), .in2(R10), .in3(R11), .in4(R12), .in5(R13), .in6(R14), .in7(R15),
    .out(multiplexer_7_out), .sel(R2_ADDRESS[2:0]));
  Multiplexer #(.select(3), .width(32), .disabled(0), .enable("false")) multiplexer_8 (
    .in0(R16), .in1(R17), .in2(R18), .in3(R19), .in4(R20), .in5(R21), .in6(R22), .in7(R23),
    .out(multiplexer_8_out), .sel(R2_ADDRESS[2:0]));
  Multiplexer #(.select(3), .width(32), .disabled(0), .enable("false")) multiplexer_9 (
    .in0(R24), .in1(R25), .in2(R26), .in3(R27), .in4(R28), .in5(R29), .in6(R30), .in7(STACK_POINTER),
    .out(multiplexer_9_out), .sel(R2_ADDRESS[2:0]));
  Register #(.width(32)) a0 (.D(DATA_IN), .en(R4_WRITE), .Q(R4), .clk(CLK), .clr(RST));
  Register #(.width(32)) t4 (.D(DATA_IN), .en(R12_WRITE), .Q(R12), .clk(CLK), .clr(RST));
  Register #(.width(32)) s4 (.D(DATA_IN), .en(R20_WRITE), .Q(R20), .clk(CLK), .clr(RST));
  Register #(.width(32)) t12 (.D(DATA_IN), .en(R28_WRITE), .Q(R28), .clk(CLK), .clr(RST));
  Multiplexer #(.select(2), .width(32), .enable("false")) multiplexer_10 (
    .in0(multiplexer_6_out), .in1(multiplexer_7_out), .in2(multiplexer_8_out), .in3(multiplexer_9_out),
    .out(R2_OUTPUT), .sel(R2_ADDRESS[4:3]));
  Register #(.width(32)) a1 (.D(DATA_IN), .en(R5_WRITE), .Q(R5), .clk(CLK), .clr(RST));
  Register #(.width(32)) t5 (.D(DATA_IN), .en(R13_WRITE), .Q(R13), .clk(CLK), .clr(RST));
  Register #(.width(32)) s5 (.D(DATA_IN), .en(R21_WRITE), .Q(R21), .clk(CLK), .clr(RST));
  Register #(.width(32)) t13 (.D(DATA_IN), .en(R29_WRITE), .Q(R29), .clk(CLK), .clr(RST));
  Register #(.width(32)) u_HIGH (.D(HIGH_INPUT), .en(HIGH_LOW_ENABLE), .Q(HIGH), .clk(CLK), .clr(RST));
  Register #(.width(32)) u_LOW (.D(DATA_IN), .en(HIGH_LOW_ENABLE), .Q(LOW), .clk(CLK), .clr(RST));
  Register #(.width(32)) a2 (.D(DATA_IN), .en(R6_WRITE), .Q(R6), .clk(CLK), .clr(RST));
  Register #(.width(32)) t6 (.D(DATA_IN), .en(R14_WRITE), .Q(R14), .clk(CLK), .clr(RST));
  Register #(.width(32)) s6 (.D(DATA_IN), .en(R22_WRITE), .Q(R22), .clk(CLK), .clr(RST));
  Register #(.width(32)) t14 (.D(DATA_IN), .en(R30_WRITE), .Q(R30), .clk(CLK), .clr(RST));
  Register #(.width(32)) a3 (.D(undriven), .en(R7_WRITE), .Q(R7), .clk(CLK), .clr(RST));
  Register #(.width(32)) t7 (.D(undriven_2), .en(R15_WRITE), .Q(R15), .clk(CLK), .clr(RST));
  Register #(.width(32)) s7 (.D(undriven_3), .en(R23_WRITE), .Q(R23), .clk(CLK), .clr(RST));
  Register #(.width(32)) SP (.D(DATA_IN), .en(R31_WRITE), .Q(STACK_POINTER), .clk(CLK), .clr(RST));

  // Other names for the same wires on the sheet: D_IN[31:0] = DATA_IN; PC_ENABLE = PROGRAM_COUNTER_ENABLE;
  //   R1_A[4:0] = R1_ADDRESS; R1_BANK_ADDRESS[2:0] = R1_ADDRESS[2:0]; R1_BANK_SELECT[1:0] = R1_ADDRESS[4:3];
  //   R1_OUT[31:0] = R1_OUTPUT; R2_A[4:0] = R2_ADDRESS; R2_BANK_ADDRESS[2:0] = R2_ADDRESS[2:0];
  //   R2_BANK_SELECT[1:0] = R2_ADDRESS[4:3]; R2_OUT[31:0] = R2_OUTPUT; BANK_ADDRESS[2:0] = RW[2:0]

  // Notes on the sheet:
  //   INPUTS
  //   REGISTER_WRITE
  //   DATA_IN
  //   WRITE_ENABLE
  //   R1_ADDRESS
  //   R2_ADDRESS
  //   HIGH_INPUT
  //   R1_OUT
  //   BANK_0
  //   BANK_2
  //   OUTPUT_BANK_SELECT
  //   BANK_SELECT
  //   REGISTER_SELECTION
  //   BANK_1
  //   BANK_3
  //   R2_OUT
  //   OUTPUTS
  //   R1_OUTPUT
  //   R2_OUTPUT
endmodule

module ALU_2 (
  input  [31:0] OP_1,
  input  [31:0] OP_2,
  input  [3:0] ALU_SELECTOR,
  output [31:0] RESULT,
  output Zero,
  output Neg
);

  Comparator #(.width(32)) comparator_1 (.a(RESULT), .b({32{1'b0}}), .eq(Zero), .lt(Neg));  // open: gt

  // Notes on the sheet:
  //   INPUTS
  //   OUTPUTS
endmodule

module Sign_Extend (
  input  [15:0] _16_Bit_Input,
  output [31:0] _32_Bit_Output
);

  Multiplexer #(.width(17)) multiplexer_1 (
    .in0({17{1'b0}}), .in1({17{1'b1}}), .out(_32_Bit_Output[31:15]), .sel(_16_Bit_Input[15]));  // open: en

  assign _32_Bit_Output[14:0] = _16_Bit_Input[14:0];
endmodule
