// Logisim project Write_Ram.circ as structural Verilog: 1 circuit, main circuit Write_Ram
module Write_Ram (
  input  [31:0] Dir_RAM,
  input  [31:0] Value,
  output [15:0] out_3,
  output [3:0] out_4,
  output [31:0] Bank_0,
  output [31:0] Bank_1,
  output [31:0] Bank_2,
  output [31:0] Bank_3
);

  wire [31:0] little_endian_to_big_endian_1_output;

  Little_Endian_to_Big_Endian little_endian_to_big_endian_1 (
    .Input(Value), .Output(little_endian_to_big_endian_1_output));
  Demultiplexer #(.select(2), .width(32), .enable("false")) demultiplexer_1 (
    .out0(Bank_0), .out1(Bank_1), .out2(Bank_2), .out3(Bank_3), .in(little_endian_to_big_endian_1_output),
    .sel(Dir_RAM[3:2]));
  Demultiplexer #(.select(2), .enable("false")) demultiplexer_2 (
    .out0(out_4[0]), .out1(out_4[1]), .out2(out_4[2]), .out3(out_4[3]), .in(1'b1), .sel(Dir_RAM[3:2]));

  assign out_3 = Dir_RAM[19:4];

  // Other names for the same wires on the sheet: Selector[1:0] = Dir_RAM[3:2]; Address[15:0] = Dir_RAM[19:4];
  //   Mask[3:0] = out_4

  // Notes on the sheet:
  //   Convert to Little Endian
endmodule
